# Fritzing sketch speaker_circuit (saved by Fritzing 0.9.3b)
breadboards: 1

parts:
  Part2 = Arduino MKR1000
  SP1 = SPEAKER [package=pcb_mount_speaker]
  R1 = Resistor [tolerance=±5% resistance=220 package="2512 [SMD]"]

nets:
  N1: Part2.GND, SP1.+
  N2: SP1.-, R1.Pin_1

custom parts:
  Arduino MKR1000: MKR1000 is a powerful board that combines the functionality of the Zero and the Wi-Fi Shield. It is the ideal solution for makers wanting to design IoT projects with minimal previous experience in networking
